# Fritzing sketch SketchArduinoHourGlass (saved by Fritzing 0.9.6b)

parts:
  Bauteil1 = Arduino Mega 2560 (Rev3)
  Bauteil2 = InvenSense MPU6050
  M2 = MAX7219 8x8 single Led Matrix Module
  M1 = MAX7219 8x8 single Led Matrix Module

nets:
  N1: Bauteil1.D21/SCL, Bauteil2.SCL
  N2: Bauteil1.D20/SDA, Bauteil2.SDA
  N3: Bauteil1.D13_PWM, M2.I-VCC, M1.I-VCC, M1.O-VCC
  N4: Bauteil1.D11_PWM, M1.I-DIN
  N5: Bauteil1.D10_PWM, M2.I-GND, M1.I-GND, M1.O-GND
  3V3: Bauteil1.3V3, Bauteil2.VCC
  N6: Bauteil1.5V, M2.I-CLK, M1.I-CLK, M1.O-CLK
  GND: Bauteil1.GND, Bauteil2.GND, M2.I-CS, M2.O-CS, M1.I-CS, M1.O-CS
  N7: M2.I-DIN, M1.O-DOUT

notes:
  VCC = Rot
  GND = Schwarz
  CL(K) = Gelb
  DA/DIN = Blau
  CS = Orange

custom parts:
  MAX7219 8x8 single Led Matrix Module: Description: MAX7219 8x8 LedMatrix single Red Module Dimensions: 32x32mm Documents:
